# Fritzing sketch Jetson Nano Passcode (saved by Fritzing 0.9.6b)
breadboards: 1

parts:
  Jetson_Nano1 = jetsonnano
  R1 = Resistor [tolerance=±5% power=0.25 resistance=220 package=THT]  # not connected
  LED1 = LED - 5mm [color="Red (633nm)" current=0.030 package="5 mm [THT]"]  # not connected
  S1 = Pushbutton [package="[THT]"]  # not connected
  S2 = Pushbutton [package="[THT]"]
  LED2 = LED - 5mm [color="Red (633nm)" current=0.030 package="5 mm [THT]"]
  LED3 = LED - 5mm [color="Red (633nm)" current=0.030 package="5 mm [THT]"]
  LED4 = LED - 5mm [color="Red (633nm)" current=0.030 package="5 mm [THT]"]
  LED5 = LED - 5mm [color="Red (633nm)" current=0.030 package="5 mm [THT]"]
  S3 = Pushbutton [package="[THT]"]
  S4 = Pushbutton [package="[THT]"]
  S5 = Pushbutton [package="[THT]"]
  R3 = Resistor [tolerance=±5% power=0.25 resistance=220 package=THT]
  R4 = Resistor [tolerance=±5% power=0.25 resistance=220 package=THT]
  R5 = Resistor [tolerance=±5% power=0.25 resistance=220 package=THT]
  R6 = Resistor [tolerance=±5% power=0.25 resistance=220 package=THT]
  LED6 = LED - 5mm [color="Red (633nm)" current=0.030 package="5 mm [THT]"]

nets:
  N1: Jetson_Nano1.connector14, LED3.anode, S4.Pin_3, S4.Pin_4, R3.Pin_0
  N2: Jetson_Nano1.connector17, LED2.cathode, LED3.cathode, LED4.cathode, LED5.cathode, R3.Pin_1, R4.Pin_1, R5.Pin_1, R6.Pin_1, LED6.cathode
  N3: Jetson_Nano1.connector20, S2.Pin_1, S2.Pin_2, S3.Pin_1, S3.Pin_2, S4.Pin_1, S4.Pin_2, S5.Pin_1, S5.Pin_2
  N4: Jetson_Nano1.connector23, LED6.anode
  N5: Jetson_Nano1.connector25, LED4.anode, S5.Pin_3, S5.Pin_4, R4.Pin_0
  N6: Jetson_Nano1.connector26, LED2.anode, S3.Pin_3, S3.Pin_4, R5.Pin_0
  N7: Jetson_Nano1.connector27, S2.Pin_3, S2.Pin_4, LED5.anode, R6.Pin_0
